# Fritzing sketch Sketch_fritzing (saved by Fritzing 0.9.3b)
breadboards: 1

parts:
  ESP32_19_pins = ESP32S-HiLetgo [part_number=ESP32S-HiLetgo]
  Module_Ethernet_W5500 = w5500 module

nets:
  N1: ESP32_19_pins.GPIO14, Module_Ethernet_W5500.Pin_4
  N2: ESP32_19_pins.GPIO12, Module_Ethernet_W5500.Pin_7
  N3: ESP32_19_pins.GPIO13, Module_Ethernet_W5500.Pin_3
  N4: ESP32_19_pins.GPIO15, Module_Ethernet_W5500.Pin_5
  N5: ESP32_19_pins.GPIO4, Module_Ethernet_W5500.Pin_6
  N6: ESP32_19_pins.GPIO5, Module_Ethernet_W5500.Pin_8
  N7: Module_Ethernet_W5500.Pin_1, Module_Ethernet_W5500.Pin_2, Module_Ethernet_W5500.Pin_12
  N8: Module_Ethernet_W5500.Pin_10, Module_Ethernet_W5500.Pin_11

custom parts:
  ESP32S-HiLetgo: HiLetgo ESP-WROOM-32 ESP32 ESP-32S Development Board 2.4GHz Dual-Mode WiFi + Bluetooth Dual Cores Microcontroller The ESP32 integrated with Antenna switches, RF Balun, power amplifiers, low-noise amplifiers, filters, and management modules, and the entire solution occupies the least area of PCB. 2.4 GHz Wi-Fi plus Bluetooth dual-mode chip, with TSMC Ultra-low power consumption 40nm technology,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
  w5500 module: MELIFE 3pcs W5500 SPI to LAN Ethernet Network Module TCP IP STM32 Interface 3.3V 5V Compatible with WIZ820io RC5.
